// Logisim project PARITY CHECKER.circ as structural Verilog: 1 circuit, main circuit main
module main (
  input  D0,
  input  D1,
  input  D2,
  input  D3,
  input  D4,
  input  D5,
  input  D6,
  input  D7,
  output U,
  output P_in
);

  wire xor_1_out, xor_2_out, xor_3_out, xor_4_out, xor_5_out, xor_6_out, xor_7_out;

  xor xor_1 (xor_1_out, D0, D1);
  xor xor_2 (xor_2_out, D2, D3);
  xor xor_3 (xor_3_out, D4, D5);
  xor xor_4 (xor_4_out, D6, D7);
  xor xor_5 (xor_5_out, xor_1_out, xor_2_out);
  xor xor_6 (xor_6_out, xor_3_out, xor_4_out);
  xor xor_7 (xor_7_out, xor_5_out, xor_6_out);
  xor xor_8 (U, xor_7_out, P_in);
endmodule
